# Fritzing sketch aquarium (saved by Fritzing 0.9.0b)
circuit board: 10cm x 6cm
breadboards: 1

parts:
  LCD1 = LCD screen
  R1 = Resistor [tolerance=±5% resistance=220 package=THT]
  Arduino_UNO = Arduino Uno (Rev3)
  R2 = Trimmer Potentiometer [maximum_resistance=10kΩ package=THT]
  S5 = Pushbutton [package="[THT]"]
  S4 = Pushbutton [package="[THT]"]
  S3 = Pushbutton [package="[THT]"]
  S2 = Pushbutton [package="[THT]"]
  S1 = Pushbutton [package="[THT]"]
  R7 = Resistor [tolerance=±5% resistance=2.2k package=THT]
  R6 = Resistor [tolerance=±5% resistance=1k package=THT]
  R5 = Resistor [tolerance=±5% resistance=680 package=THT]
  R4 = Resistor [tolerance=±5% resistance=330 package=THT]
  R3 = Resistor [tolerance=±5% resistance=2k package=THT]
  R11 = Resistor [tolerance=±5% resistance=1k package=THT]
  R12 = Resistor [tolerance=±5% resistance=1k package=THT]
  R13 = Resistor [tolerance=±5% resistance=1k package=THT]
  R14 = Resistor [tolerance=±5% resistance=1k package=THT]
  DHT1 = DHT11 Humitidy and Temperature Sensor
  D1 = LED_BARGRAPH_10 [package=led_bargaph_10]
  RTC1 = DS1307 RTC Breakout
  J1 = Piezo Speaker

nets (from the breadboard view):
  GND: LCD1.VSS, LCD1.R/W, LCD1.LED-, Arduino_UNO.GND, R2.leg1, S5.Pin_1, S5.Pin_2, S4.Pin_1, S4.Pin_2, S3.Pin_1, S3.Pin_2, S2.Pin_1, S2.Pin_2, S1.Pin_1, S1.Pin_2, R11.Pin_0, R12.Pin_0, R13.Pin_0, R14.Pin_0, DHT1.GND, RTC1.GND, J1.pin1
  VDD: LCD1.VDD, R1.Pin_0, Arduino_UNO.5V, R2.leg2, R3.Pin_0, DHT1.VDD, RTC1.5V
  N1: LCD1.V0, R2.wiper
  N2: LCD1.RS, Arduino_UNO.D13/SCK
  N3: LCD1.E, Arduino_UNO.D12/MISO
  N4: LCD1.DB4, Arduino_UNO.D5_PWM
  N5: LCD1.DB5, Arduino_UNO.D4
  N6: LCD1.DB6, Arduino_UNO.D3_PWM
  N7: LCD1.DB7, Arduino_UNO.D2
  N8: LCD1.LED+, R1.Pin_1
  N9: Arduino_UNO.A0, DHT1.DATA
  N10: Arduino_UNO.A1, S1.Pin_3, S1.Pin_4, R4.Pin_0, R3.Pin_1
  N11: Arduino_UNO.A5/SCL, RTC1.SCL
  N12: Arduino_UNO.D8, D1.H_C
  N13: Arduino_UNO.D9_PWM, D1.F_C
  N14: Arduino_UNO.D10_PWM/SS, D1.B_C
  N15: Arduino_UNO.D11_PWM/MOSI, D1.C_C
  N16: Arduino_UNO.A4/SDA, RTC1.SDA
  N17: Arduino_UNO.D7, J1.pin2
  N18: S5.Pin_3, S5.Pin_4, R7.Pin_1
  N19: S4.Pin_3, S4.Pin_4, R7.Pin_0, R6.Pin_1
  N20: S3.Pin_3, S3.Pin_4, R6.Pin_0, R5.Pin_1
  N21: S2.Pin_3, S2.Pin_4, R5.Pin_0, R4.Pin_1
  N22: R11.Pin_1, D1.A_A
  N23: R12.Pin_1, D1.C_A
  N24: R13.Pin_1, D1.F_A
  N25: R14.Pin_1, D1.H_A, D1.I_A

custom parts:
  DHT11 Humitidy and Temperature Sensor: DHT11 Humidity and Temperature Sensor
  DS1307 RTC Breakout: DS1307 Real-time Clock Breakout Board with Battery
